// Logisim project hbcpu.circ as structural Verilog: 8 circuits, main circuit main
module main (
  input  A,
  input  B,
  input  C,
  input  nG2AEn,
  input  nG2BEn,
  input  G1En,
  output nY0,
  output nY1,
  output nY2,
  output nY3,
  output nY4,
  output nY5,
  output nY6,
  output nY7
);

  _74138 u_74138_1 (
    .pin1(A), .pin2(B), .pin3(C), .pin4(nG2AEn), .pin5(nG2BEn), .pin6(G1En), .pin7(nY7), .pin15(nY0),
    .pin14(nY1), .pin13(nY2), .pin12(nY3), .pin11(nY4), .pin10(nY5), .pin9(nY6));

  // Notes on the sheet:
  //   3-line to 8-line decoder
endmodule

module LeftShift (
  input  [7:0] A,
  input  [7:0] B,
  input  [1:0] OP,
  input  CI,
  output [7:0] O,
  output [7:0] out_6,
  output CO,
  output out_8
);

  wire and_1_out, and_3_out, C, n7404_1_pin5, n7404_1_pin6, n7404_1_pin8, n7404_1_pin9, n7404_1_pin10,
       n7404_1_pin11, n7404_1_pin12, n7404_1_pin13, n7408_1_pin3, n7408_1_pin6, n7408_1_pin11, n7408_1_pin12,
       n7408_1_pin13, n7408_2_pin1, n7408_2_pin2, n7408_2_pin3, n7408_2_pin5, n7432_1_pin3, n7432_1_pin8,
       n7432_1_pin9, n7432_1_pin10, n7432_1_pin11, n7432_1_pin12, n7432_1_pin13, nB1, nB2,
       pull_resistor_1_node, S1_CO, S2_CO, S4_CO;
  wire [7:0] S1, S1_O, S2, S2_O;

  // NoConnect on OP[1]
  // NoConnect on B[7:3]
  Multiplexer multiplexer_1 (.in0(CI), .in1(pull_resistor_1_node), .out(C), .sel(OP[0]));
  Pull_Resistor pull_resistor_1 (.node(pull_resistor_1_node));
  _74157 u_74157_1 (
    .pin1(B[0]), .pin2(A[0]), .pin3(C), .pin4(S1[0]), .pin5(A[1]), .pin6(A[0]), .pin7(S1[1]), .pin14(A[4]),
    .pin13(A[3]), .pin12(S1[4]), .pin11(A[5]), .pin10(A[4]), .pin9(S1[5]));  // open: pin15
  _74157 u_74157_2 (
    .pin1(B[2]), .pin2(S2[0]), .pin3(C), .pin4(out_6[0]), .pin5(S2[1]), .pin6(C), .pin7(out_6[1]),
    .pin14(S2[4]), .pin13(S2[0]), .pin12(out_6[4]), .pin11(S2[5]), .pin10(S2[1]), .pin9(out_6[5]));  // open: pin15
  // NoConnect on n7404_1_pin13
  _7404 u_7404_1 (
    .pin1(B[1]), .pin2(nB1), .pin3(B[2]), .pin4(nB2), .pin5(n7404_1_pin5), .pin6(n7404_1_pin6),
    .pin13(n7404_1_pin13), .pin12(n7404_1_pin12), .pin11(n7404_1_pin11), .pin10(n7404_1_pin10),
    .pin9(n7404_1_pin9), .pin8(n7404_1_pin8));
  // NoConnect on n7404_1_pin12
  // NoConnect on n7404_1_pin11
  // NoConnect on n7404_1_pin10
  // NoConnect on n7404_1_pin9
  // NoConnect on n7404_1_pin5
  // NoConnect on n7404_1_pin6
  _74157 u_74157_3 (
    .pin1(B[0]), .pin2(A[2]), .pin3(A[1]), .pin4(S1[2]), .pin5(A[3]), .pin6(A[2]), .pin7(S1[3]),
    .pin14(A[6]), .pin13(A[5]), .pin12(S1[6]), .pin11(A[7]), .pin10(A[6]), .pin9(S1[7]));  // open: pin15
  _74157 u_74157_4 (
    .pin1(B[2]), .pin2(S2[2]), .pin3(C), .pin4(out_6[2]), .pin5(S2[3]), .pin6(C), .pin7(out_6[3]),
    .pin14(S2[6]), .pin13(S2[2]), .pin12(out_6[6]), .pin11(S2[7]), .pin10(S2[3]), .pin9(out_6[7]));  // open: pin15
  // NoConnect on n7404_1_pin8
  // NoConnect on n7408_1_pin13
  // NoConnect on n7408_1_pin12
  _7408 u_7408_1 (
    .pin1(nB1), .pin2(nB2), .pin3(n7408_1_pin3), .pin4(n7408_1_pin3), .pin5(B[0]), .pin6(n7408_1_pin6),
    .pin13(n7408_1_pin13), .pin12(n7408_1_pin12), .pin11(n7408_1_pin11), .pin10(A[7]), .pin9(n7408_1_pin6),
    .pin8(S1_CO));
  Multiplexer #(.width(8)) multiplexer_2 (.in0(A), .in1({A[6:0], C}), .out({S1_O[7], S1[6], S1_O[5:0]}), .sel(B[0]));
  and and_1 (and_1_out, ~B[2], ~B[1], B[0]);  // AND_Gate
  // NoConnect on n7408_1_pin11
  and and_2 (S1_CO, A[7], and_1_out);
  Multiplexer #(.width(8)) multiplexer_3 (
    .in0({S1_O[7], S1[6], S1_O[5:0]}), .in1({S1_O[5:0], {2{C}}}), .out({S2_O[7:5], S2[4], S2_O[3:0]}),
    .sel(B[1]));
  // NoConnect on S1_O[7]
  and and_3 (and_3_out, ~B[2], B[1]);  // AND_Gate
  _7408 u_7408_2 (
    .pin1(n7408_2_pin1), .pin2(n7408_2_pin2), .pin3(n7408_2_pin3), .pin4(S1[6]), .pin5(n7408_2_pin5),
    .pin6(S2_CO), .pin13(S2[4]), .pin12(B[2]), .pin11(S4_CO), .pin10(nB2), .pin9(B[1]), .pin8(n7408_2_pin5));
  // NoConnect on n7408_2_pin1
  // NoConnect on n7408_2_pin2
  // NoConnect on n7408_2_pin3
  and and_4 (S2_CO, S1[6], and_3_out);
  _74157 u_74157_5 (
    .pin1(B[1]), .pin2(S1[0]), .pin3(C), .pin4(S2[0]), .pin5(S1[1]), .pin6(C), .pin7(S2[1]), .pin14(S1[4]),
    .pin13(S1[2]), .pin12(S2[4]), .pin11(S1[5]), .pin10(S1[3]), .pin9(S2[5]));  // open: pin15
  // NoConnect on S2_O[5]
  // NoConnect on S2_O[6]
  // NoConnect on S2_O[7]
  and and_5 (S4_CO, S2[4], B[2]);
  Multiplexer #(.width(8)) multiplexer_4 (
    .in0({S2_O[7:5], S2[4], S2_O[3:0]}), .in1({S2_O[3:0], {4{C}}}), .out(O), .sel(B[2]));
  _74157 u_74157_6 (
    .pin1(B[1]), .pin2(S1[2]), .pin3(S1[0]), .pin4(S2[2]), .pin5(S1[3]), .pin6(S1[1]), .pin7(S2[3]),
    .pin14(S1[6]), .pin13(S1[4]), .pin12(S2[6]), .pin11(S1[7]), .pin10(S1[5]), .pin9(S2[7]));  // open: pin15
  // NoConnect on n7432_1_pin13
  _7432 u_7432_1 (
    .pin1(S1_CO), .pin2(S2_CO), .pin3(n7432_1_pin3), .pin4(n7432_1_pin3), .pin5(S4_CO), .pin6(out_8),
    .pin13(n7432_1_pin13), .pin12(n7432_1_pin12), .pin11(n7432_1_pin11), .pin10(n7432_1_pin10),
    .pin9(n7432_1_pin9), .pin8(n7432_1_pin8));
  or or_1 (CO, S1_CO, S2_CO, S4_CO);
  // NoConnect on n7432_1_pin12
  // NoConnect on n7432_1_pin11
  // NoConnect on n7432_1_pin10
  // NoConnect on n7432_1_pin9
  // NoConnect on n7432_1_pin8

  // Other names for the same wires on the sheet: S1_C = A[7]; S1_0 = S1[0]; S1_1 = S1[1]; S1_2 = S1[2]; S1_3 = S1[3];
  //   S1_4 = S1[4]; S1_5 = S1[5]; S1_6 = S1[6]; S1_O[6] = S1[6]; S2_C = S1[6]; S1_7 = S1[7]; S2_0 = S2[0];
  //   S2_1 = S2[1]; S2_2 = S2[2]; S2_3 = S2[3]; S2_4 = S2[4]; S2_O[4] = S2[4]; S4_C = S2[4]; S2_5 = S2[5];
  //   S2_6 = S2[6]; S2_7 = S2[7]; S4[7:0] = out_6; S4_0 = out_6[0]; S4_1 = out_6[1]; S4_2 = out_6[2]; S4_3 = out_6[3];
  //   S4_4 = out_6[4]; S4_5 = out_6[5]; S4_6 = out_6[6]; S4_7 = out_6[7]
endmodule

module RightShift (
  input  [7:0] A,
  input  [7:0] B,
  input  ARITH,
  output [7:0] O,
  output COut
);

  wire and_2_out, and_3_out, and_4_out, and_5_out, or_1_out, or_2_out, or_3_out, or_4_out;
  wire [7:0] multiplexer_1_out, multiplexer_2_out, multiplexer_3_out;
  wire [7:7] and_1_out;

  or or_1 (or_1_out, A[0], A[1], A[2], A[3]);
  and and_1 (and_1_out[7], A[7], ARITH);
  Multiplexer #(.width(8)) multiplexer_1 (
    .in0(A), .in1({{4{and_1_out[7]}}, A[7:4]}), .out(multiplexer_1_out), .sel(B[2]));
  and and_2 (and_2_out, or_1_out, B[2]);
  or or_2 (or_2_out, multiplexer_1_out[0], multiplexer_1_out[1]);
  Multiplexer #(.width(8)) multiplexer_2 (
    .in0(multiplexer_1_out), .in1({{2{and_1_out[7]}}, multiplexer_1_out[7:2]}), .out(multiplexer_2_out),
    .sel(B[1]));
  and and_3 (and_3_out, or_2_out, B[1]);
  Multiplexer #(.width(8)) multiplexer_3 (
    .in0(multiplexer_2_out), .in1({and_1_out[7], multiplexer_2_out[7:1]}), .out(multiplexer_3_out), .sel(B[0]));
  and and_4 (and_4_out, multiplexer_2_out[0], B[0]);
  or or_3 (or_3_out, B[7], B[6], B[5], B[4], B[3]);
  or or_4 (or_4_out, A[0], A[1], A[2], A[3], A[4], A[5], A[6], A[7]);
  Multiplexer #(.width(8)) multiplexer_4 (.in0(multiplexer_3_out), .in1({8{and_1_out[7]}}), .out(O), .sel(or_3_out));
  and and_5 (and_5_out, or_3_out, or_4_out);
  or or_5 (COut, and_4_out, and_3_out, and_2_out, and_5_out);

  // Notes on the sheet:
  //   Right Shift
endmodule

module ALU (
  input  [7:0] A,
  input  [7:0] B,
  input  CI,
  input  [3:0] OP,
  output [7:0] O,
  output CO
);

  wire SL_CO, undriven_2, undriven_3, undriven_4;
  wire [7:0] ADDER_O, LO, SL_O, SR_O, undriven;

  LeftShift leftshift_1 (.A(A), .B(B), .OP(OP[3:2]), .CI(CI), .O(SL_O), .CO(SL_CO));  // open: out_6, out_8
  RightShift rightshift_1 (.A(undriven), .O(SR_O));  // open: B, ARITH, COut
  AluAdder aluadder_1 ();  // open: CIn, OP, A, B, O, COut
  AluLogic alulogic_1 ();  // open: A, B, OP, O
  Multiplexer #(.select(2), .width(8)) multiplexer_1 (
    .in0(SL_O), .in1(SR_O), .in2(ADDER_O), .in3(LO), .out(O), .sel(OP[1:0]));
  Multiplexer #(.select(2)) multiplexer_2 (
    .in0(SL_CO), .in1(undriven_2), .in2(undriven_3), .in3(undriven_4), .out(CO), .sel(OP[1:0]));

  // Other names for the same wires on the sheet: Unit[1:0] = OP[1:0]; OP_t[1:0] = OP[3:2]
endmodule

module Adder8Bit (
  input  CIn,
  input  [7:0] A,
  input  [7:0] B,
  output [7:0] O,
  output COut
);

  wire adder1bit_1_cout, adder1bit_2_cout, adder1bit_3_cout, adder1bit_4_cout, adder1bit_5_cout,
       adder1bit_6_cout, adder1bit_7_cout;

  Adder1Bit adder1bit_1 (.A(A[0]), .B(B[0]), .CIn(CIn), .O(O[0]), .COut(adder1bit_1_cout));
  Adder1Bit adder1bit_2 (.A(A[1]), .B(B[1]), .CIn(adder1bit_1_cout), .O(O[1]), .COut(adder1bit_2_cout));
  Adder1Bit adder1bit_3 (.A(A[2]), .B(B[2]), .CIn(adder1bit_2_cout), .O(O[2]), .COut(adder1bit_3_cout));
  Adder1Bit adder1bit_4 (.A(A[3]), .B(B[3]), .CIn(adder1bit_3_cout), .O(O[3]), .COut(adder1bit_4_cout));
  Adder1Bit adder1bit_5 (.A(A[4]), .B(B[4]), .CIn(adder1bit_4_cout), .O(O[4]), .COut(adder1bit_5_cout));
  Adder1Bit adder1bit_6 (.A(A[5]), .B(B[5]), .CIn(adder1bit_5_cout), .O(O[5]), .COut(adder1bit_6_cout));
  Adder1Bit adder1bit_7 (.A(A[6]), .B(B[6]), .CIn(adder1bit_6_cout), .O(O[6]), .COut(adder1bit_7_cout));
  Adder1Bit adder1bit_8 (.A(A[7]), .B(B[7]), .CIn(adder1bit_7_cout), .O(O[7]), .COut(COut));
endmodule

module Adder1Bit (
  input  A,
  input  B,
  input  CIn,
  output O,
  output COut
);

  wire and_1_out, and_2_out, xor_1_out;

  xor xor_1 (xor_1_out, A, B);
  and and_1 (and_1_out, A, B);
  xor xor_2 (O, xor_1_out, CIn);
  and and_2 (and_2_out, xor_1_out, CIn);
  or or_1 (COut, and_1_out, and_2_out);
endmodule

module AluLogic (
  input  [7:0] A,
  input  [7:0] B,
  input  [1:0] OP,
  output [7:0] O
);

  wire [7:0] and_1_out, not_1_out, or_1_out, xor_1_out;

  assign and_1_out = A & B;  // AND_Gate and_1, 8 bits wide
  assign or_1_out = A | B;  // OR_Gate or_1, 8 bits wide
  assign xor_1_out = A ^ B;  // XOR_Gate xor_1, 8 bits wide
  assign not_1_out = ~A;  // NOT_Gate not_1, 8 bits wide
  Multiplexer #(.select(2), .width(8)) multiplexer_1 (
    .in0(and_1_out), .in1(or_1_out), .in2(xor_1_out), .in3(not_1_out), .out(O), .sel(OP));
endmodule

module AluAdder (
  input  CIn,
  input  [1:0] OP,
  input  [7:0] A,
  input  [7:0] B,
  output [7:0] O,
  output COut
);

  wire multiplexer_1_out, pull_resistor_1_node, pull_resistor_2_node;
  wire [7:0] multiplexer_2_out, not_1_out;

  Pull_Resistor #(.pull(1)) pull_resistor_1 (.node(pull_resistor_1_node));
  Pull_Resistor pull_resistor_2 (.node(pull_resistor_2_node));
  Multiplexer #(.select(2)) multiplexer_1 (
    .in0(pull_resistor_2_node), .in1(pull_resistor_1_node), .in2(CIn), .in3(CIn), .out(multiplexer_1_out),
    .sel(OP));
  assign not_1_out = ~B;  // NOT_Gate not_1, 8 bits wide
  // NoConnect on OP[1]
  Multiplexer #(.width(8)) multiplexer_2 (.in0(B), .in1(not_1_out), .out(multiplexer_2_out), .sel(OP[0]));
  Adder8Bit adder8bit_1 (.CIn(multiplexer_1_out), .A(A), .B(multiplexer_2_out), .O(O), .COut(COut));

  // Notes on the sheet:
  //   00 ADD
  //   01 SUB
  //   10 ADDC
  //   11 SUBB
endmodule
